// Logisim project lab3.circ as structural Verilog
module traffic_light (
);

  wire clock_1_out;
  wire [2:0] rom_1_data;
  wire [4:0] counter_1_q;

  Counter #(.max('h1f), .width(5)) counter_1 (
    .clk(clock_1_out), .Q(counter_1_q));  // open: clr, load, up, count, D, carry
  Clock clock_1 (.out(clock_1_out));
  ROM #(.addrWidth(5), .dataWidth(3)) rom_1 (.addr(counter_1_q), .data(rom_1_data));
  LED led_1 (.in(rom_1_data[0]));
  LED led_2 (.in(rom_1_data[1]));
  LED led_3 (.in(rom_1_data[2]));

  // Notes on the sheet:
  //   contents of rom_1 (hex, n*v repeats v):
  //   12*1 4*4 15*2
endmodule

module assignment (
);

  wire clock_1_out, twodigitcircuit_1_out_5, twodigitcircuit_1_out_6, twodigitcircuit_1_out_7,
       twodigitcircuit_1_out_8, twodigitcircuit_1_out_9, twodigitcircuit_1_out_10, twodigitcircuit_1_out_11,
       twodigitcircuit_1_out_12, twodigitcircuit_1_out_13, twodigitcircuit_1_out_14,
       twodigitcircuit_1_out_15, twodigitcircuit_1_out_16, twodigitcircuit_1_out_17,
       twodigitcircuit_1_out_18, twodigitcircuit_2_out_5, twodigitcircuit_2_out_6, twodigitcircuit_2_out_7,
       twodigitcircuit_2_out_8, twodigitcircuit_2_out_9, twodigitcircuit_2_out_10, twodigitcircuit_2_out_11,
       twodigitcircuit_2_out_12, twodigitcircuit_2_out_13, twodigitcircuit_2_out_14,
       twodigitcircuit_2_out_15, twodigitcircuit_2_out_16, twodigitcircuit_2_out_17,
       twodigitcircuit_2_out_18, twodigitcircuit_3_out_5, twodigitcircuit_3_out_6, twodigitcircuit_3_out_7,
       twodigitcircuit_3_out_8, twodigitcircuit_3_out_9, twodigitcircuit_3_out_10, twodigitcircuit_3_out_11,
       twodigitcircuit_3_out_12, twodigitcircuit_3_out_13, twodigitcircuit_3_out_14,
       twodigitcircuit_3_out_15, twodigitcircuit_3_out_16, twodigitcircuit_3_out_17,
       twodigitcircuit_3_out_18, twodigitcircuit_4_out_5, twodigitcircuit_4_out_6, twodigitcircuit_4_out_7,
       twodigitcircuit_4_out_8, twodigitcircuit_4_out_9, twodigitcircuit_4_out_10, twodigitcircuit_4_out_11,
       twodigitcircuit_4_out_12, twodigitcircuit_4_out_13, twodigitcircuit_4_out_14,
       twodigitcircuit_4_out_15, twodigitcircuit_4_out_16, twodigitcircuit_4_out_17, twodigitcircuit_4_out_18;
  wire [2:0] rom_1_data, rom_2_data, rom_3_data, rom_4_data;
  wire [4:0] counter_1_q;

  twodigitcircuit twodigitcircuit_1 (
    .in_1(counter_1_q[4]), .in_2(counter_1_q[3]), .in_3(counter_1_q[2]), .in_4(counter_1_q[1]),
    .out_5(twodigitcircuit_1_out_5), .out_6(twodigitcircuit_1_out_6), .out_7(twodigitcircuit_1_out_7),
    .out_8(twodigitcircuit_1_out_8), .out_9(twodigitcircuit_1_out_9), .out_10(twodigitcircuit_1_out_10),
    .out_11(twodigitcircuit_1_out_11), .out_12(twodigitcircuit_1_out_12), .out_13(twodigitcircuit_1_out_13),
    .out_14(twodigitcircuit_1_out_14), .out_15(twodigitcircuit_1_out_15), .out_16(twodigitcircuit_1_out_16),
    .out_17(twodigitcircuit_1_out_17), .out_18(twodigitcircuit_1_out_18));
  twodigitcircuit twodigitcircuit_2 (
    .out_5(twodigitcircuit_2_out_5), .out_6(twodigitcircuit_2_out_6), .out_7(twodigitcircuit_2_out_7),
    .out_8(twodigitcircuit_2_out_8), .out_9(twodigitcircuit_2_out_9), .out_10(twodigitcircuit_2_out_10),
    .out_11(twodigitcircuit_2_out_11), .out_12(twodigitcircuit_2_out_12), .out_13(twodigitcircuit_2_out_13),
    .out_14(twodigitcircuit_2_out_14), .out_15(twodigitcircuit_2_out_15), .out_16(twodigitcircuit_2_out_16),
    .out_17(twodigitcircuit_2_out_17), .out_18(twodigitcircuit_2_out_18));  // open: in_1, in_2, in_3, in_4
  ROM #(.addrWidth(5), .dataWidth(3)) rom_1 (.addr(counter_1_q), .data(rom_1_data));
  _7_Segment_Display u_7_segment_display_1 (
    .g(twodigitcircuit_1_out_11), .f(twodigitcircuit_1_out_8), .a(twodigitcircuit_1_out_5),
    .b(twodigitcircuit_1_out_6), .e(twodigitcircuit_1_out_9), .d(twodigitcircuit_1_out_10),
    .c(twodigitcircuit_1_out_7));  // open: dp
  _7_Segment_Display u_7_segment_display_2 (
    .g(twodigitcircuit_2_out_11), .f(twodigitcircuit_2_out_8), .a(twodigitcircuit_2_out_5),
    .b(twodigitcircuit_2_out_6), .e(twodigitcircuit_2_out_9), .d(twodigitcircuit_2_out_10),
    .c(twodigitcircuit_2_out_7));  // open: dp
  _7_Segment_Display u_7_segment_display_3 (
    .g(twodigitcircuit_2_out_18), .f(twodigitcircuit_2_out_17), .a(twodigitcircuit_2_out_12),
    .b(twodigitcircuit_2_out_13), .e(twodigitcircuit_2_out_16), .d(twodigitcircuit_2_out_15),
    .c(twodigitcircuit_2_out_14));  // open: dp
  _7_Segment_Display u_7_segment_display_4 (
    .g(twodigitcircuit_1_out_18), .f(twodigitcircuit_1_out_17), .a(twodigitcircuit_1_out_12),
    .b(twodigitcircuit_1_out_13), .e(twodigitcircuit_1_out_16), .d(twodigitcircuit_1_out_15),
    .c(twodigitcircuit_1_out_14));  // open: dp
  ROM #(.addrWidth(5), .dataWidth(3)) rom_2 (.addr(counter_1_q), .data(rom_2_data));
  LED led_1 (.in(rom_1_data[0]));
  LED led_2 (.in(rom_1_data[1]));
  LED led_3 (.in(rom_1_data[2]));
  Counter #(.max('h1f), .width(5)) counter_1 (
    .clk(clock_1_out), .Q(counter_1_q));  // open: clr, load, up, count, D, carry
  Clock clock_1 (.out(clock_1_out));
  LED led_4 (.in(rom_2_data[0]));
  LED led_5 (.in(rom_2_data[1]));
  LED led_6 (.in(rom_2_data[2]));
  ROM #(.addrWidth(5), .dataWidth(3)) rom_3 (.addr(counter_1_q), .data(rom_3_data));
  ROM #(.addrWidth(5), .dataWidth(3)) rom_4 (.addr(counter_1_q), .data(rom_4_data));
  LED led_7 (.in(rom_4_data[0]));
  LED led_8 (.in(rom_4_data[1]));
  LED led_9 (.in(rom_4_data[2]));
  LED led_10 (.in(rom_3_data[0]));
  LED led_11 (.in(rom_3_data[1]));
  LED led_12 (.in(rom_3_data[2]));
  twodigitcircuit twodigitcircuit_3 (
    .out_5(twodigitcircuit_3_out_5), .out_6(twodigitcircuit_3_out_6), .out_7(twodigitcircuit_3_out_7),
    .out_8(twodigitcircuit_3_out_8), .out_9(twodigitcircuit_3_out_9), .out_10(twodigitcircuit_3_out_10),
    .out_11(twodigitcircuit_3_out_11), .out_12(twodigitcircuit_3_out_12), .out_13(twodigitcircuit_3_out_13),
    .out_14(twodigitcircuit_3_out_14), .out_15(twodigitcircuit_3_out_15), .out_16(twodigitcircuit_3_out_16),
    .out_17(twodigitcircuit_3_out_17), .out_18(twodigitcircuit_3_out_18));  // open: in_1, in_2, in_3, in_4
  twodigitcircuit twodigitcircuit_4 (
    .out_5(twodigitcircuit_4_out_5), .out_6(twodigitcircuit_4_out_6), .out_7(twodigitcircuit_4_out_7),
    .out_8(twodigitcircuit_4_out_8), .out_9(twodigitcircuit_4_out_9), .out_10(twodigitcircuit_4_out_10),
    .out_11(twodigitcircuit_4_out_11), .out_12(twodigitcircuit_4_out_12), .out_13(twodigitcircuit_4_out_13),
    .out_14(twodigitcircuit_4_out_14), .out_15(twodigitcircuit_4_out_15), .out_16(twodigitcircuit_4_out_16),
    .out_17(twodigitcircuit_4_out_17), .out_18(twodigitcircuit_4_out_18));  // open: in_1, in_2, in_3, in_4
  _7_Segment_Display u_7_segment_display_5 (
    .g(twodigitcircuit_3_out_11), .f(twodigitcircuit_3_out_8), .a(twodigitcircuit_3_out_5),
    .b(twodigitcircuit_3_out_6), .e(twodigitcircuit_3_out_9), .d(twodigitcircuit_3_out_10),
    .c(twodigitcircuit_3_out_7));  // open: dp
  _7_Segment_Display u_7_segment_display_6 (
    .g(twodigitcircuit_3_out_18), .f(twodigitcircuit_3_out_17), .a(twodigitcircuit_3_out_12),
    .b(twodigitcircuit_3_out_13), .e(twodigitcircuit_3_out_16), .d(twodigitcircuit_3_out_15),
    .c(twodigitcircuit_3_out_14));  // open: dp
  _7_Segment_Display u_7_segment_display_7 (
    .g(twodigitcircuit_4_out_11), .f(twodigitcircuit_4_out_8), .a(twodigitcircuit_4_out_5),
    .b(twodigitcircuit_4_out_6), .e(twodigitcircuit_4_out_9), .d(twodigitcircuit_4_out_10),
    .c(twodigitcircuit_4_out_7));  // open: dp
  _7_Segment_Display u_7_segment_display_8 (
    .g(twodigitcircuit_4_out_18), .f(twodigitcircuit_4_out_17), .a(twodigitcircuit_4_out_12),
    .b(twodigitcircuit_4_out_13), .e(twodigitcircuit_4_out_16), .d(twodigitcircuit_4_out_15),
    .c(twodigitcircuit_4_out_14));  // open: dp

  // Notes on the sheet:
  //   contents of rom_1 (hex, n*v repeats v):
  //   12*2 4*4 16*1
  //   contents of rom_2 (hex, n*v repeats v):
  //   16*1 12*2 4*4
  //   contents of rom_3 (hex, n*v repeats v):
  //   12*2 4*4 16*1
  //   contents of rom_4 (hex, n*v repeats v):
  //   16*1 12*2 4*4
endmodule

module segment (
  input  a,
  input  b,
  input  c,
  input  d,
  output e,
  output f,
  output g,
  output h,
  output i,
  output j,
  output k,
  output l,
  output m,
  output n,
  output o,
  output p,
  output q,
  output r
);

  wire and_1_out, and_2_out, and_3_out, and_4_out, and_5_out, and_6_out, and_7_out, and_8_out, and_9_out,
       and_10_out, and_11_out, and_12_out, and_13_out, and_14_out, and_15_out, and_16_out, and_17_out,
       and_18_out, and_19_out, and_20_out, and_21_out, and_22_out, and_23_out, and_24_out, and_25_out,
       and_26_out, and_27_out, and_28_out, and_29_out, and_30_out, and_31_out, and_32_out, not_1_out,
       not_2_out, not_3_out, not_4_out;

  not not_1 (not_1_out, a);
  not not_2 (not_2_out, b);
  not not_3 (not_3_out, c);
  not not_4 (not_4_out, d);
  and and_1 (and_1_out, a, c);
  and and_2 (and_2_out, a, b);
  and and_3 (and_3_out, a, c);
  and and_4 (and_4_out, a, b);
  and and_5 (and_5_out, a, c);
  and and_6 (and_6_out, a, b);
  and and_7 (and_7_out, a, c);
  and and_8 (and_8_out, a, b);
  and and_9 (and_9_out, not_1_out, not_3_out);
  and and_10 (and_10_out, a, not_4_out);
  and and_11 (and_11_out, c, d);
  and and_12 (and_12_out, a, b);
  and and_13 (and_13_out, not_1_out, c);
  and and_14 (and_14_out, a, not_3_out);
  and and_15 (and_15_out, not_1_out, d);
  or or_1 (n, not_2_out, not_3_out, not_4_out, a);
  and and_16 (and_16_out, not_1_out, not_3_out);
  and and_17 (and_17_out, b, d);
  and and_18 (and_18_out, a, c);
  and and_19 (and_19_out, not_1_out, d);
  and and_20 (and_20_out, a, not_2_out, not_4_out);
  and and_21 (and_21_out, not_1_out, not_2_out, not_3_out, not_4_out);
  and and_22 (and_22_out, c, d);
  and and_23 (and_23_out, b, d);
  and and_24 (and_24_out, not_2_out, c);
  and and_25 (and_25_out, a, d);
  and and_26 (and_26_out, a, c);
  and and_27 (and_27_out, not_1_out, not_3_out, not_4_out);
  and and_28 (and_28_out, not_1_out, b, not_3_out);
  and and_29 (and_29_out, not_1_out, not_3_out, not_4_out);
  and and_30 (and_30_out, not_1_out, c, d);
  and and_31 (and_31_out, a, not_3_out, d);
  and and_32 (and_32_out, a, c, not_4_out);
  or or_2 (e, and_1_out, and_2_out);
  or or_3 (h, and_3_out, and_4_out);
  or or_4 (i, and_5_out, and_6_out);
  or or_5 (j, and_7_out, and_8_out);
  or or_6 (l, and_9_out, and_10_out, and_11_out, and_12_out);
  or or_7 (m, and_13_out, b, and_14_out, and_15_out);
  or or_8 (o, and_16_out, and_17_out, and_18_out, and_19_out, and_20_out);
  or or_9 (p, and_21_out, and_22_out, and_23_out);
  or or_10 (q, and_24_out, and_25_out, and_26_out, and_27_out, and_28_out);
  or or_11 (r, not_2_out, and_29_out, and_30_out, and_31_out, and_32_out);

  assign f = 1'b1;
  assign g = 1'b1;
  assign k = 1'b0;
endmodule

module twodigitcircuit (
  input  in_1,
  input  in_2,
  input  in_3,
  input  in_4,
  output out_5,
  output out_6,
  output out_7,
  output out_8,
  output out_9,
  output out_10,
  output out_11,
  output out_12,
  output out_13,
  output out_14,
  output out_15,
  output out_16,
  output out_17,
  output out_18
);

  segment segment_1 (
    .a(in_1), .b(in_2), .c(in_3), .d(in_4), .e(out_5), .f(out_6), .g(out_7), .h(out_8), .i(out_9),
    .j(out_10), .k(out_11), .l(out_12), .m(out_13), .n(out_14), .o(out_15), .p(out_16), .q(out_17), .r(out_18));
endmodule
