// Logisim project project.circ as structural Verilog: 3 circuits, main circuit main
module main (
  input  in_1,
  input  in_2,
  input  in_3,
  input  in_4,
  input  in_5,
  input  in_6,
  output out_7,
  output out_8
);

  wire segment_1_e, segment_1_f, segment_1_g, segment_1_h, segment_1_j, segment_1_k, segment_1_l;

  addition addition_1 (.a(in_5), .b(in_6), .sum(out_7), .Carry(out_8));
  segment segment_1 (
    .a(in_1), .b(in_2), .c(in_3), .d(in_4), .e(segment_1_e), .f(segment_1_f), .g(segment_1_g),
    .h(segment_1_h), .j(segment_1_j), .k(segment_1_k), .l(segment_1_l));
  _7_Segment_Display u_7_segment_display_1 (
    .g(segment_1_l), .f(segment_1_k), .a(segment_1_e), .b(segment_1_f), .e(segment_1_j), .d(segment_1_h),
    .c(segment_1_g));  // open: dp
endmodule

module segment (
  input  a,
  input  b,
  input  c,
  input  d,
  output e,
  output f,
  output g,
  output h,
  output j,
  output k,
  output l
);

  wire and_1_out, and_2_out, and_3_out, and_4_out, and_5_out, and_6_out, and_7_out, and_8_out, and_9_out,
       and_10_out, and_11_out, and_12_out, and_13_out, and_14_out, and_15_out, and_16_out, and_17_out,
       and_18_out, not_1_out, not_2_out, not_3_out;

  not not_1 (not_1_out, b);
  not not_2 (not_2_out, c);
  not not_3 (not_3_out, d);
  and and_1 (and_1_out, not_1_out, not_3_out);
  and and_2 (and_2_out, b, d);
  and and_3 (and_3_out, not_2_out, not_3_out);
  and and_4 (and_4_out, c, d);
  or or_1 (g, not_2_out, d, b);
  and and_5 (and_5_out, not_1_out, not_3_out);
  and and_6 (and_6_out, not_1_out, c);
  and and_7 (and_7_out, b, not_2_out, d);
  and and_8 (and_8_out, c, not_3_out);
  and and_9 (and_9_out, not_1_out, not_3_out);
  and and_10 (and_10_out, c, not_3_out);
  and and_11 (and_11_out, a, c);
  and and_12 (and_12_out, a, b);
  and and_13 (and_13_out, not_2_out, not_3_out);
  and and_14 (and_14_out, b, not_2_out);
  and and_15 (and_15_out, b, not_3_out);
  and and_16 (and_16_out, not_1_out, c);
  and and_17 (and_17_out, b, not_2_out);
  and and_18 (and_18_out, c, not_3_out);
  or or_2 (e, and_1_out, c, and_2_out, a);
  or or_3 (f, not_1_out, and_3_out, and_4_out);
  or or_4 (h, and_5_out, and_6_out, and_7_out, and_8_out, a);
  or or_5 (j, and_9_out, and_10_out, and_11_out, and_12_out);
  or or_6 (k, and_13_out, and_14_out, and_15_out, a);
  or or_7 (l, and_16_out, and_17_out, a, and_18_out);
endmodule

module addition (
  input  a,
  input  b,
  output sum,
  output Carry
);

  xor xor_1 (sum, a, b);
  and and_1 (Carry, a, b);
endmodule
